# Fritzing sketch obstaculos 2.0 (saved by Fritzing 0.9.2b)
circuit board: 8.63998cm x 7.34906cm
breadboards: 1

parts:
  R2 = Resistor [tolerance=±5% resistance=10k package=THT]
  Componente1 = SRF05 Ultrasonic Rangefinder
  Componente2 = SRF05 Ultrasonic Rangefinder
  Componente3 = SRF05 Ultrasonic Rangefinder
  Q2 = MOSFET-NCHANNEL [package=to-92]
  R3 = Resistor [tolerance=±5% resistance=10k package=THT]
  R4 = Resistor [tolerance=±5% resistance=10k package=THT]
  Q3 = MOSFET-NCHANNEL [package=to-92]
  R5 = Resistor [tolerance=±5% resistance=10k package=THT]
  R6 = Resistor [tolerance=±5% resistance=10k package=THT]
  Q4 = MOSFET-NCHANNEL [package=to-92]
  R7 = Resistor [tolerance=±5% resistance=10k package=THT]
  R8 = Resistor [tolerance=±5% resistance=10k package=THT]
  J3 = OLED pins [form="♀ (female)" package=THT]
  Q1 = MOSFET-NCHANNEL [package=to-92]
  5V = screw terminal, 2 pins
  R1 = Resistor [tolerance=±5% resistance=10k package=THT]
  J5 = female pin header, 15 pins [form="♀ (female)"]
  J6 = female pin header, 1 pin [form="♀ (female)"]
  J7 = female pin header, 1 pin [form="♀ (female)"]
  J8 = female pin header, 1 pin [form="♀ (female)"]
  J9 = female pin header, 1 pin [form="♀ (female)"]
  J10 = female pin header, 15 pins [form="♀ (female)"]
  J12 = female pin header, 15 pins [form="♀ (female)"]
  J11 = female pin header, 10 pins [form="♀ (female)"]
  3_3V = screw terminal, 2 pins
  J80 = female pin header, 6 pins [form="♀ (female)"]
  J81 = female pin header, 6 pins [form="♀ (female)"]
  5V1 = screw terminal, 2 pins
  J82 = female pin header, 6 pins [form="♀ (female)"]
  5V2 = screw terminal, 2 pins

nets:
  N1: R2.Pin_0, Q1.S, J8.pin1
  N2: R2.Pin_1, Q2.G, R4.Pin_1, Q3.G, R6.Pin_1, Q4.G, R8.Pin_1, Q1.G, J6.pin1, 3_3V.pin1
  N3: Componente1.Trig, Componente2.Trig, Componente3.Trig, Q1.D, R1.Pin_0
  VCC: Componente1.VCC, Componente2.VCC, Componente3.VCC, R3.Pin_1, R5.Pin_1, R7.Pin_1, 5V.pin2, R1.Pin_1, J5.pin1, J12.pin1, J81.pin3, J82.pin3
  N4: Componente1.Echo, Q3.D, R5.Pin_0
  GND: Componente1.GND, Componente2.GND, Componente3.GND, 5V.pin1, J5.pin2, J12.pin2, 3_3V.pin2, J81.pin4, J82.pin4
  N5: Componente2.Echo, Q4.D, R7.Pin_0
  N6: Componente3.Echo, Q2.D, R3.Pin_0
  N7: Q2.S, R4.Pin_0, J9.pin1
  N8: Q3.S, R6.Pin_0
  N9: Q4.S, R8.Pin_0, J7.pin1
  N10: J3.GND, J10.pin2, J11.pin2
  N11: J3.VCC, J10.pin1, J11.pin1
  N12: J3.SCL, J10.pin14
  N13: J3.SDA, J10.pin11
  N14: J5.pin3, J12.pin3
  N15: J5.pin4, J12.pin4
  N16: J5.pin5, J12.pin5
  N17: J5.pin6, J12.pin6
  N18: J5.pin7, J12.pin7
  N19: J5.pin8, J12.pin8
  N20: J5.pin9, J12.pin9
  N21: J5.pin10, J12.pin10
  N22: J5.pin11, J12.pin11
  N23: J5.pin12, J12.pin12
  N24: J5.pin13, J12.pin13
  N25: J5.pin14, J12.pin14
  N26: J5.pin15, J12.pin15
  N27: J10.pin3, J11.pin3
  N28: J10.pin4, J11.pin4
  N29: J10.pin5, J11.pin5
  N30: J10.pin6, J11.pin6
  N31: J10.pin7, J11.pin7
  N32: J10.pin8, J11.pin8
  N33: J10.pin9, J11.pin9
  N34: J10.pin10, J11.pin10
  N35: J80.pin2, 5V1.pin2
  N36: J80.pin3, 5V1.pin1
  N37: J80.pin4, 5V2.pin2
  N38: J80.pin5, 5V2.pin1
  N39: J81.pin1, J82.pin1
  N40: J81.pin2, J82.pin2
  N41: J81.pin5, J82.pin5
  N42: J81.pin6, J82.pin6

notes:
  Motor 1
  Motor 2
  ESP32
  Ponte H

custom parts:
  OLED pins: Female pins named for OLED display.
