# Fritzing sketch pcb_dimmer (saved by Fritzing 0.9.2b)
circuit board: 4.33552cm x 2.53564cm
breadboards: 1

parts:
  DB1 = DIAC Diode [part_number=DB3 package=DO-35]
  R1 = Resistor [tolerance=±5% resistance=22k package=THT]
  J2 = Screw terminal - 2 pins [package=THT]
  J1 = Screw terminal - 2 pins [package=THT]
  R2 = Resistor [tolerance=±5% resistance=10k package=THT]
  C6 = Capacitor [part_number=47nF package=cap-pth-5mm]
  U1 = TRIAC [package=sot223]
  470K = POT [package=pot_alpha_rv16af-20]
  C5 = Capacitor [part_number=47nF package=cap-pth-5mm]

nets:
  N1: DB1.Anode_1, U1.G
  N2: DB1.Anode_2, R2.Pin_1, C5.2
  N3: R1.Pin_0, 470K.E
  N4: R1.Pin_1, J2.pin2, J1.pin1
  N5: J2.pin1, C6.1, U1.M1, C5.1
  N6: J1.pin2, U1.M2
  N7: R2.Pin_0, 470K.S
  N8: C6.2, 470K.A

notes:
  Marina Rocha e Luiza Lopes, 3E
  Placa Dimmer - Eletrônica Industrial
  Borne conectado à linha de alimentação
  Borne ligado à lâmpada
  Borne conectado na rede
