# Fritzing sketch pcb_neopixel (saved by Fritzing 0.9.2b)
circuit board: 4.36601cm x 3.52489cm
breadboards: 1

parts:
  S3 = Pushbutton [package="[THT]"]
  S4 = Pushbutton [package="[THT]"]
  U3 = ESP8266 WiFi Module [part_number=ESP8266]
  R8 = Resistor [tolerance=±5% resistance=3.3k package=THT]
  R10 = Resistor [tolerance=±5% resistance=3.3k package=THT]
  J2 = screw terminal, 2 pins
  R7 = Resistor [tolerance=±5% resistance=3.3k package=THT]
  R6 = Resistor [tolerance=±5% resistance=150 package=THT]
  LED2 = LED - 5mm [color="Red (633nm)" package="5 mm [THT]"]
  R9 = Resistor [tolerance=±5% resistance=3.3k package=THT]
  J11 = Neopixel [form="♀ (female)" package=THT]

nets:
  GND: S3.Pin_3, S3.Pin_4, S4.Pin_1, S4.Pin_2, U3.GPIO_0, U3.RST, U3.GND, R10.Pin_0, J2.pin1, R9.Pin_0, J11.GND
  VCC: U3.VCC, R8.Pin_1, R10.Pin_1, J2.pin2, R7.Pin_1, R6.Pin_1, R9.Pin_1, J11.VCC
  N1: U3.GPIO_2, R7.Pin_0, LED2.cathode
  N2: U3.CH_PD, R8.Pin_0
  N3: U3.TXD, J11.OUT
  N4: R6.Pin_0, LED2.anode

notes:
  150Ω
  3.3kΩ

custom parts:
  ESP8266 WiFi Module: Generic WiFi Module based on the ESP8266 with onboard PCB antenna and UART communications
  Neopixel: Neopixel - LED RGB
